# Fritzing sketch light_panel (saved by Fritzing 1.0.6)
circuit board: 6.08558cm x 2.86671cm
breadboards: 1

parts:
  J3 = double row female pin header, 16 pins [form="♀ (female)"]
  M1 = DOIT Esp32 DevKit v1 (30 pins long, 11 pins width) [part_number=ESP32S-PIN30]
  J2 = molex pin header, 4 pins [form=molex]

nets:
  N1: J3.pin2, M1.RX2
  N2: J3.pin3, M1.TX2
  N3: J3.pin4, M1.D5
  N4: J3.pin6, M1.D19
  N5: J3.pin8, M1.D21
  N6: J3.pin9, M1.D18
  N7: J3.pin10, M1.D4
  N8: J3.pin11, M1.D32
  N9: J3.pin12, M1.D33
  N10: J3.pin13, M1.D25
  N11: J3.pin14, M1.D26
  N12: J3.pin15, M1.D27
  N13: J3.pin16, M1.D14
  N14: M1.VIN, J2.pin1, J2.pin2

notes:
  The LED Art Panel
  Designed in San Francisco
  for teaching and learning.

custom parts:
  DOIT Esp32 DevKit v1 (30 pins long, 11 pins width): The DOIT Esp32 DevKit v1 is one of the development board created by DOIT to evaluate the ESP-WROOM-32 module. It is based on the ESP32 microcontroller that boasts Wifi, Bluetooth, Ethernet and Low Power support all in a single chip. (vanepp) made breadboard work, adjusted pin numbering and labels and reduced size of schematic and cleaned up pcb. This chip is 30pins long (2 x15) and 11 pins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
